# Fritzing sketch thermostatElectronicDesign (saved by Fritzing 0.9.3b)
breadboards: 2

parts:
  VCC1 = Battery block 9V
  U8 = Voltage Regulator - 3.3V [part_number=LM1086IT package="TO220 [THT]"]
  U9 = Voltage Regulator - 5V [part_number=L7805CV package="TO220 [THT]"]
  C12 = Tantalum Capacitor [capacitance="1 μF" package="B 3528 [SMD, tantalum]"]
  C15 = Ceramic Capacitor [capacitance=330nF voltage=50V package="0805 [SMD, multilayer]"]
  C16 = Ceramic Capacitor [capacitance=100nF voltage=50V package="100 mil [THT, multilayer]"]
  D2 = Diode [package=diode-1n4001]
  U10 = RELAY [package=relay-t9a-2]
  C17 = Tantalum Capacitor [capacitance="1 μF" package="B 3528 [SMD, tantalum]"]
  R7 = Resistor [tolerance=±5% resistance=1k package=THT]
  R8 = Resistor [tolerance=±5% resistance=1k package=THT]
  LED2 = LED - 5mm [color="Yellow (595nm)" package="5 mm [THT]"]
  LED3 = LED - 5mm [color="Yellow (595nm)" package="5 mm [THT]"]
  Q5 = NPN-Transistor [package="SOT-23 [SMD]"]
  R9 = Resistor [tolerance=±5% resistance=1k package=THT]
  D5 = Diode [package=diode-1n4001]  # not connected
  S2 = Toggle Switch [package=THT]
  D6 = Diode [package=diode-1n4001]
  Composant3 = Arduino Nano (Rev3.0) (ICSP)
  MOD-WIFI-ESP8266-DEV2 = Olimex ESP8266 DEV
  LCD2 = LCD screen
  LCM1602_IIC2 = LCM1602 IIC [part_number="LCM1602 IIC" chip_label="LCM1602 IIC" package="DIP (Dual Inline) [THT]"]
  Composant4 = FTDI Basic Programmer
  R10 = Resistor [tolerance=±5% resistance=1k part_number=R10 package=THT]
  R11 = Resistor [tolerance=±5% resistance=2.2k part_number=R11 package=THT]
  U11 = RELAY [package=relay-t9a-2]
  R12 = Resistor [tolerance=±5% resistance=1k part_number=R14 package=THT]
  LED4 = LED - 5mm [color="Blue (525nm)" package="5 mm [THT]"]
  R13 = Resistor [tolerance=±5% resistance=1k part_number=R17 package=THT]
  LED5 = LED - 5mm [color="Yellow (585nm)" package="5 mm [THT]"]
  IR2 = TSOP312.., 314.. [part_number=AX-1838HS package=THT]
  DS2 = DS18B20 1-Wire Temperature Sensor [part_number=DS18B20]
  R14 = Resistor [tolerance=±5% resistance=4.7k part_number=R13 package=THT]
  D7 = Diode [part_number=D10 package=diode-hv]
  LED6 = LED - 5mm [color="Red (633nm)" package="5 mm [THT]"]
  R15 = Resistor [tolerance=±5% resistance=1k part_number=R16 package=THT]
  Q6 = PNP-Transistor [part_number=T10 package="TO92 [THT]"]
  Composant6 = Real Time Clock Module - DS1307 RTC Breakout Board [part_number=MR005]
  R16 = Resistor [tolerance=±5% resistance=1k part_number=R15 package=THT]
  S6 = Toggle Switch [part_number=Sw10 package=THT]
  R17 = Resistor [tolerance=±5% resistance=10k part_number=R12 package=THT]
  S7 = Pushbutton [part_number=Pb10 package="[THT]"]

nets:
  GND: VCC1.-, U9.GND, C12.+, C15.0, C16.1, U10.COIL2, C17.-, R8.Pin_0, LED3.cathode, Q5.1, Composant3.RESET, Composant3.GND, Composant3.D11/MOSI, MOD-WIFI-ESP8266-DEV2.GND, LCM1602_IIC2.GND, Composant4.GND, R11.Pin_1, U11.COIL2, LED4.cathode, LED5.cathode, IR2.GND, DS2.GND, LED6.cathode, Q6.E, Composant6.GND, S6.L2, S7.Pin_3, S7.Pin_4
  N1: VCC1.+, D2.A, D6.A, Composant3.VIN
  N2: U8.Output, C17.+, R7.Pin_0
  N3: U8.input_voltage, C12.-, S2.COM
  N4: U9.input_voltage, C15.1
  VCC: U9.output_voltage, C16.0, LED2.anode, LCM1602_IIC2.VCC, LCM1602_IIC2.SDA, IR2.Vs, Composant6.5V
  N5: U10.MAIN, S2.L2
  N6: U10.NC, S2.L1
  N7: R7.Pin_1, LED3.anode
  N8: R8.Pin_1, LED2.cathode
  N9: Q5.0, R9.Pin_0
  N10: Composant3.D1/TX, R10.Pin_0
  N11: Composant3.D4, IR2.Data
  N12: Composant3.D6, R13.Pin_1
  N13: Composant3.D7, R12.Pin_1, LED4.anode
  N14: Composant3.D8, DS2.DQ, R14.Pin_1
  N15: Composant3.D10, R15.Pin_1, R16.Pin_0
  5V: Composant3.5V, DS2.VDD, R14.Pin_0
  N16: Composant3.A5, LCM1602_IIC2.SCL, Composant6.SQW, Composant6.SCL
  N17: Composant3.A4, Composant6.SDA
  N18: MOD-WIFI-ESP8266-DEV2.GPIO1, Composant4.RXI
  N19: MOD-WIFI-ESP8266-DEV2.GPIO3, Composant4.TXO
  N20: MOD-WIFI-ESP8266-DEV2.GPIO5, R12.Pin_0
  N21: MOD-WIFI-ESP8266-DEV2.GPIO0, S7.Pin_1, S7.Pin_2
  N22: MOD-WIFI-ESP8266-DEV2.GPIO4, S6.COM
  VSS: LCD2.VSS, LCM1602_IIC2.VSS
  VDD: LCD2.VDD, LCM1602_IIC2.VDD
  N23: LCD2.V0, LCM1602_IIC2.V0
  N24: LCD2.RS, LCM1602_IIC2.RS
  N25: LCD2.R/W, LCM1602_IIC2.RW
  N26: LCD2.E, LCM1602_IIC2.E
  N27: LCD2.DB0, LCM1602_IIC2.D0
  N28: LCD2.DB1, LCM1602_IIC2.D1
  N29: LCD2.DB2, LCM1602_IIC2.D2
  N30: LCD2.DB3, LCM1602_IIC2.D3
  N31: LCD2.DB4, LCM1602_IIC2.D4
  N32: LCD2.DB5, LCM1602_IIC2.D5
  N33: LCD2.DB6, LCM1602_IIC2.D6
  N34: LCD2.DB7, LCM1602_IIC2.D7
  N35: LCD2.LED+, LCM1602_IIC2.A
  N36: LCD2.LED-, LCM1602_IIC2.K
  N37: R10.Pin_1, R11.Pin_0
  N38: R13.Pin_0, LED5.anode
  N39: D7.A, Q6.C
  N40: LED6.anode, R15.Pin_0
  N41: Q6.B, R16.Pin_1
  N42: S6.L1, R17.Pin_1

notes:
  +3.3V
  +5V
  +9v
  +3.3v
  > to boiler

custom parts:
  Voltage Regulator - 3.3V: 3.3V DC Voltage Regulator
  Olimex ESP8266 DEV: MOD-WIFI-ESP8266-DEV is the ultimate development board for ESP8266 with all GPIOs and resources exposed, can be soldered to PCB or used with breadboard and UEXT. Small U.FL connector is provided for external antenna connection. ESP8266 is very highly integrated SOC which includes Xtensa LX106 core processor, RAM, RF front end and allow WIFI TCP-IP stack to be implemented on board with just few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
  LCM1602 IIC: I2C-Module to use a 1602 or 2004 LCD on with the wire.h libory Serial LCD Modul
