# Fritzing sketch thermostatPower (saved by Fritzing 0.9.3b)
circuit board: 8.46667cm x 5.64444cm
breadboards: 1

parts:
  VCC1 = Battery block 9V
  U8 = Voltage Regulator - 3.3V [part_number=LM1086IT package="TO220 [THT]"]
  U9 = Voltage Regulator - 5V [part_number=L7805CV package="TO220 [THT]"]
  C12 = Tantalum Capacitor [capacitance="1 μF" part_number=C2 package="B 3528 [SMD, tantalum]"]
  C15 = Ceramic Capacitor [capacitance=330nF voltage=50V part_number=C3 package="0805 [SMD, multilayer]"]
  C16 = Ceramic Capacitor [capacitance=100nF voltage=50V part_number=C4 package="100 mil [THT, multilayer]"]
  D2 = Diode [part_number=D2 package=diode-1n4001]
  U10 = RELAY [package=relay-t9a-2]
  C17 = Tantalum Capacitor [capacitance="1 μF" part_number=C1 package="B 3528 [SMD, tantalum]"]
  R7 = Resistor [tolerance=±5% resistance=1k part_number=R3 package=THT]
  R8 = Resistor [tolerance=±5% resistance=1k part_number=R2 package=THT]
  LED2 = LED - 5mm [color="Yellow (595nm)" part_number=L2 package="5 mm [THT]"]
  LED3 = LED - 5mm [color="Yellow (595nm)" part_number=L1 package="5 mm [THT]"]
  Q5 = NPN-Transistor [part_number=T1 package="SOT-23 [SMD]"]
  R9 = Resistor [tolerance=±5% resistance=1k part_number=R1 package=THT]
  D5 = Diode [part_number=Di1 package=diode-1n4001]  # not connected
  D6 = Diode [part_number=D3 package=diode-1n4001]
  S2 = Toggle Switch [part_number=Sw1 package=THT]

nets:
  N1: VCC1.-, U9.GND, C12.+, C15.0, C16.1, U10.COIL2, C17.-, R8.Pin_0, LED3.cathode, Q5.1
  N2: VCC1.+, D2.A, D6.A
  N3: U8.Output, C17.+, R7.Pin_0
  N4: U8.input_voltage, C12.-, S2.COM
  N5: U9.input_voltage, C15.1
  N6: U9.output_voltage, C16.0, LED2.anode
  N7: U10.MAIN, S2.L2
  N8: U10.NC, S2.L1
  N9: R7.Pin_1, LED3.anode
  N10: R8.Pin_1, LED2.cathode
  N11: Q5.0, R9.Pin_0

notes:
  Regulated +3.3V > to ESP8266 VIN
  Regulated+5V > to 5v PCB
  not regulated 9v > to Arduino VIN
  > to Arduino GPIO
  The switch is used to deliver 3.3v before GPIO connection

custom parts:
  Voltage Regulator - 3.3V: 3.3V DC Voltage Regulator
